# Fritzing sketch Шаблон электросхемы проекта-теплинский (saved by Fritzing 0.9.3b)
breadboards: 1

parts:
  VCC1 = Battery
  S1 = Toggle Switch [package=THT]
  Part3 = Arduino Uno (Rev3) - ICSP
  Part4 = RFID-RC522-v2
  LED1 = LED - 5mm [color="Red (633nm)" package="5 mm [THT]"]
  J1 = Basic Servo
  R1 = Resistor [tolerance=±5% resistance=220 package=THT]

nets:
  N1: VCC1.-, S1.L1
  N2: VCC1.+, J1.vcc
  GND: S1.L2, Part3.GND, Part4.GND, J1.gnd, R1.Pin_1
  N3: Part3.ICSP_MOSI, Part3.D11_PWM/MOSI, Part4.MOSI
  N4: Part3.D9_PWM, Part4.RST
  N5: Part3.D10_PWM/SS, Part4.SDA
  N6: Part3.D12/MISO, Part4.MISO
  N7: Part3.D13/SCK, Part4.SCK
  N8: Part3.D2, J1.pulse
  N9: Part3.D3_PWM, LED1.cathode
  N10: Part3.3V3, Part4.3_3V
  N11: LED1.anode, R1.Pin_0

custom parts:
  RFID-RC522-v2: A simple China made RFID-RC522 Reader; do check the pin labels, as this is a MFRC522 based clone.
